# Fritzing sketch IrRemote (saved by Fritzing 0.9.9b)
breadboards: 1

parts:
  Parça1 = BluePill
  R1 = Resistor [tolerance=±5% power=0.25 resistance=10k package=THT]
  S1 = Pushbutton [package="[THT]"]
  S2 = Pushbutton [package="[THT]"]
  S3 = Pushbutton [package="[THT]"]
  S4 = Pushbutton [package="[THT]"]
  S5 = Pushbutton [package="[THT]"]
  S6 = Pushbutton [package="[THT]"]
  R3 = Resistor [tolerance=±5% power=0.25 resistance=220 package=THT]
  R4 = Resistor [tolerance=±5% power=0.25 resistance=220 package=THT]
  R5 = Resistor [tolerance=±5% power=0.25 resistance=10k package=THT]
  R6 = Resistor [tolerance=±5% power=0.25 resistance=220 package=THT]
  R7 = Resistor [tolerance=±5% power=0.25 resistance=10k package=THT]
  R8 = Resistor [tolerance=±5% power=0.25 resistance=220 package=THT]
  R9 = Resistor [tolerance=±5% power=0.25 resistance=10k package=THT]
  R10 = Resistor [tolerance=±5% power=0.25 resistance=220 package=THT]
  R11 = Resistor [tolerance=±5% power=0.25 resistance=10k package=THT]
  R12 = Resistor [tolerance=±5% power=0.25 resistance=220 package=THT]
  R13 = Resistor [tolerance=±5% power=0.25 resistance=10k package=THT]
  LED1 = LED - 5mm [color="Yellow (585nm)" current=0.030 package="5 mm [THT]"]
  LED2 = LED - 5mm [color="Blue (505nm)" current=0.030 package="5 mm [THT]"]
  IR1 = TSOP312.., 314.. [package=THT]
  LED3 = Photodiode 5mm Black [package="5 mm [THT]"]
  R14 = Resistor [tolerance=±5% power=0.25 resistance=220 package=THT]
  R15 = Resistor [tolerance=±5% power=0.25 resistance=220 package=THT]

nets:
  N1: Parça1.A0, S6.Pin_1, S6.Pin_2, R13.Pin_0
  N2: Parça1.A1, S5.Pin_1, S5.Pin_2, R11.Pin_0
  N3: Parça1.A4, S4.Pin_1, S4.Pin_2, R9.Pin_0
  N4: Parça1.A5, S3.Pin_1, S3.Pin_2, R7.Pin_0
  N5: Parça1.A6, S1.Pin_1, S1.Pin_2, R5.Pin_0
  N6: Parça1.A7, R1.Pin_1, S2.Pin_1, S2.Pin_2
  N7: Parça1.B0, IR1.Data
  N8: Parça1.B10, R14.Pin_1
  N9: Parça1.B11, R15.Pin_1
  N10: Parça1.3V3, R3.Pin_0, R4.Pin_1, R7.Pin_1, R8.Pin_1, R11.Pin_1, R12.Pin_1, IR1.Vs
  GND2: Parça1.GND2, R1.Pin_0, R5.Pin_1, R6.Pin_1, R9.Pin_1, R10.Pin_1, R13.Pin_1, LED1.cathode, LED2.cathode, IR1.GND, LED3.cathode
  N11: Parça1.B1, LED3.anode
  N12: S1.Pin_3, S1.Pin_4, R4.Pin_0
  N13: S2.Pin_3, S2.Pin_4, R3.Pin_1
  N14: S3.Pin_3, S3.Pin_4, R6.Pin_0
  N15: S4.Pin_3, S4.Pin_4, R8.Pin_0
  N16: S5.Pin_3, S5.Pin_4, R10.Pin_0
  N17: S6.Pin_3, S6.Pin_4, R12.Pin_0
  N18: LED1.anode, R15.Pin_0
  N19: LED2.anode, R14.Pin_0

notes:
  A0:Recieve Moda geçiş butonu
  A1:Down Button
  A4:Right Button
  A5:Button Ok
  A6:Button Left
  A7:Button Up
  B10:(Blue Led) Transmit moda gecince lojik 1 olur
  B11:(Yellow Led) Reciever moda gecince loji1 1 olur
  B1 :Ir transmitter led'e bağlı
  B0: Ir Reciever çıkışına bağlı

custom parts:
  Photodiode 5mm Black: Photodiode 5mm Black/ Transparent
